// Logisim project ALSU.circ as structural Verilog: 3 circuits, main circuit Bit16_ALSU
module Bit16_ALSU (
  input  [15:0] A,
  input  [15:0] B,
  input  [3:0] S,
  input  C_prev,
  output [15:0] F,
  output C_next
);

  wire shiftleft_1_o_next, shiftleft_2_o_next, shiftright_1_o_prev;
  wire [15:0] and_1_out, and_2_out, and_3_out, and_4_out, bit16_arithmatic_unit_1_c_next,
       bit16_arithmatic_unit_1_d, bit16_logic_unit_1_yi, bit_extender_1_out, bit_extender_2_out, not_1_out,
       not_2_out, shiftleft_1_o, shiftleft_2_o, shiftright_1_o;

  ShiftLeft shiftleft_1 (
    .I_prev(C_prev), .I(bit16_arithmatic_unit_1_c_next), .O(shiftleft_1_o), .O_next(shiftleft_1_o_next));
  ShiftLeft shiftleft_2 (.I_prev(C_prev), .I(A), .O(shiftleft_2_o), .O_next(shiftleft_2_o_next));
  ShiftRight shiftright_1 (.I(A), .I_next(C_prev), .O_prev(shiftright_1_o_prev), .O(shiftright_1_o));
  Bit16_Arithmatic_Unit bit16_arithmatic_unit_1 (
    .A(A), .B(B), .S0(S[0]), .S1(S[1]), .C_prev(shiftleft_1_o), .C_next(bit16_arithmatic_unit_1_c_next),
    .D(bit16_arithmatic_unit_1_d));
  Bit16_Logic_Unit bit16_logic_unit_1 (.A(A), .B(B), .S0(S[0]), .S1(S[1]), .Yi(bit16_logic_unit_1_yi));
  Mux4x1 mux4x1_1 (
    .I0(shiftleft_1_o_next), .I1(1'b0), .I2(shiftleft_2_o_next), .I3(shiftright_1_o_prev), .S1(S[3]),
    .S0(S[2]), .Y(C_next));
  assign not_1_out = ~bit_extender_1_out;  // NOT_Gate not_1, 16 bits wide
  assign bit_extender_1_out = {{15{S[2]}}, S[2]};  // Bit_Extender bit_extender_1
  assign bit_extender_2_out = {{15{S[3]}}, S[3]};  // Bit_Extender bit_extender_2
  assign not_2_out = ~bit_extender_2_out;  // NOT_Gate not_2, 16 bits wide
  assign and_1_out = bit16_arithmatic_unit_1_d & not_1_out & not_2_out;  // AND_Gate and_1, 16 bits wide
  assign and_2_out = bit16_logic_unit_1_yi & bit_extender_1_out & not_2_out;  // AND_Gate and_2, 16 bits wide
  assign and_3_out = shiftleft_2_o & not_1_out & bit_extender_2_out;  // AND_Gate and_3, 16 bits wide
  assign and_4_out = shiftright_1_o & bit_extender_1_out & bit_extender_2_out;  // AND_Gate and_4, 16 bits wide
  assign F = and_1_out | and_2_out | and_3_out | and_4_out;  // OR_Gate or_1, 16 bits wide

  // Notes on the sheet:
  //   A_prev
  //   A_next
  //   C_prev
  //   ALSU For Moris Mano Machine
  //   ALSU is just a combinational circuit that performs all the provided operations, and the one required is chosen.
  //   Mux 4x1 couldn't be imported here.
endmodule

module ShiftRight (
  input  [15:0] I,
  input  I_next,
  output O_prev,
  output [15:0] O
);


  assign O = {I_next, I[15:1]};
  assign O_prev = I[0];
endmodule

module ShiftLeft (
  input  I_prev,
  input  [15:0] I,
  output [15:0] O,
  output O_next
);


  assign O = {I[14:0], I_prev};
  assign O_next = I[15];
endmodule
