// Logisim project Control_Unit.circ as structural Verilog: 1 circuit, main circuit Control_Unit
module Control_Unit (
  input  [15:0] IR,
  input  R,
  input  IEN,
  input  FGI,
  input  FGO,
  input  [3:0] SC,
  input  CLR,
  output [3:0] ALUS,
  output ALUCin,
  output SCCLR,
  output ACLD,
  output ACINR,
  output ACCLR,
  output ARLD,
  output ARINR,
  output ARCLR,
  output DRLD,
  output DRINC,
  output DRCLR,
  output IRLD,
  output IRCLR,
  output READ,
  output WRITE,
  output PCLD,
  output PCINR,
  output PCCLR,
  output TRLD,
  output TRINR,
  output TRCLR,
  output ARE,
  output PCE,
  output DRE,
  output ACE,
  output IRE,
  output TRE,
  output MEME,
  output ELD,
  output ECLR,
  output ECMP,
  output IENSET,
  output IENCLR,
  output SCLR,
  output RSET,
  output RCLR,
  output FGICLR,
  output FGOCLR,
  output CPE
);

  wire and_1_out, and_2_out, not_1_out;
  wire [8:1] decoder3x8_1_p11;
  wire [15:0] decoder4x16_1_p20;

  // Decoder3x8 decoder3x8_1: pin names not known; wires that end beside it: decoder3x8_1_p11[8], decoder3x8_1_p11[7], decoder3x8_1_p11[6], decoder3x8_1_p11[5], decoder3x8_1_p11[4], IR[14], decoder3x8_1_p11[3], IR[13], decoder3x8_1_p11[2], IR[12], decoder3x8_1_p11[1]
  // Decoder4x16 decoder4x16_1: pin names not known; wires that end beside it: decoder4x16_1_p20[15], SC[0], decoder4x16_1_p20[14], SC[1], decoder4x16_1_p20[13], SC[2], decoder4x16_1_p20[12], SC[3], decoder4x16_1_p20[11], decoder4x16_1_p20[10], decoder4x16_1_p20[9], decoder4x16_1_p20[8], decoder4x16_1_p20[7], decoder4x16_1_p20[6], decoder4x16_1_p20[5], decoder4x16_1_p20[4], decoder4x16_1_p20[3], decoder4x16_1_p20[2], decoder4x16_1_p20[1], decoder4x16_1_p20[0]
  and and_1 (and_1_out, decoder3x8_1_p11[8], IR[15], decoder4x16_1_p20[12]);
  not not_1 (not_1_out, IR[15]);
  and and_2 (and_2_out, decoder3x8_1_p11[8], not_1_out, decoder4x16_1_p20[12]);
  ALSU_ControlUnit alsu_controlunit_1 (
    .B7(IR[7]), .B6(IR[6]), .D0(decoder3x8_1_p11[1]), .B9(IR[9]), .D2(decoder3x8_1_p11[3]),
    .T5(decoder4x16_1_p20[10]), .r(and_2_out), .S(ALUS), .Cin(ALUCin));  // open: B5
  SC_ControlUnit sc_controlunit_1 (
    .R(R), .T2(decoder4x16_1_p20[13]), .s_r(and_2_out), .p(and_1_out), .D6(decoder3x8_1_p11[7]),
    .T6(decoder4x16_1_p20[9]), .T4(decoder4x16_1_p20[11]), .D3(decoder3x8_1_p11[4]),
    .D4(decoder3x8_1_p11[5]), .T5(decoder4x16_1_p20[10]), .D0(decoder3x8_1_p11[1]), .D1(decoder3x8_1_p11[2]),
    .D2(decoder3x8_1_p11[3]), .D5(decoder3x8_1_p11[6]), .CLR(CLR), .SCCLR(SCCLR));
  AC_ControlUnit ac_controlunit_1 (
    .D0(decoder3x8_1_p11[1]), .D1(decoder3x8_1_p11[2]), .D2(decoder3x8_1_p11[3]), .T5(decoder4x16_1_p20[10]),
    .p(and_1_out), .r(and_2_out), .B9(IR[9]), .B7(IR[7]), .B6(IR[6]), .B5(IR[5]), .B11(IR[11]), .CLR(CLR),
    .ACLD(ACLD), .ACINR(ACINR), .ACCLR(ACCLR));
  AR_ControlUnit ar_controlunit_1 (
    .D7(decoder3x8_1_p11[8]), .I(IR[15]), .T3(decoder4x16_1_p20[12]), .T2(decoder4x16_1_p20[13]), .R(R),
    .T0(decoder4x16_1_p20[15]), .D5(decoder3x8_1_p11[6]), .T4(decoder4x16_1_p20[11]), .CLR(CLR), .ARLD(ARLD),
    .ARINR(ARINR), .ARCLR(ARCLR));
  DR_ControlUnit dr_controlunit_1 (
    .D0(decoder3x8_1_p11[1]), .D1(decoder3x8_1_p11[2]), .D2(decoder3x8_1_p11[3]), .D6(decoder3x8_1_p11[7]),
    .T4(decoder4x16_1_p20[11]), .T5(decoder4x16_1_p20[10]), .CLR(CLR), .DRLD(DRLD), .DRINC(DRINC),
    .DRCLR(DRCLR));
  IR_ControlUnit ir_controlunit_1 (.R(R), .T1(decoder4x16_1_p20[14]), .CLR(CLR), .IRLD(IRLD), .IRCLR(IRCLR));
  Mem_ControlUnit mem_controlunit_1 (
    .D7(decoder3x8_1_p11[8]), .I(IR[15]), .T3(decoder4x16_1_p20[12]), .R(R), .T1(decoder4x16_1_p20[14]),
    .D0(decoder3x8_1_p11[1]), .D1(decoder3x8_1_p11[2]), .D2(decoder3x8_1_p11[3]), .D6(decoder3x8_1_p11[7]),
    .T4(decoder4x16_1_p20[11]), .T6(decoder4x16_1_p20[9]), .D5(decoder3x8_1_p11[6]),
    .D3(decoder3x8_1_p11[4]), .READ(READ), .WRITE(WRITE));
  PC_ControlUnit pc_controlunit_1 (
    .D4(decoder3x8_1_p11[5]), .T4(decoder4x16_1_p20[11]), .D5(decoder3x8_1_p11[6]),
    .T5(decoder4x16_1_p20[10]), .R(R), .T1(decoder4x16_1_p20[14]), .T2(and_1_out), .B4(IR[11]),
    .AC_15(IR[9]), .B3(IR[5]), .AC_equals_0(CLR), .FGO(R), .D6(decoder4x16_1_p20[15]), .T6(CLR), .PCLD(PCLD),
    .PCINR(PCINR), .PCCLR(PCCLR));  // open: B2, E_equals_0, B1, s_r, p, B9, FGI, B8, DR_equals_0, CLR
  TR_ControlUnit tr_controlunit_1 (
    .R(R), .T0(decoder4x16_1_p20[15]), .CLR(CLR), .TRLD(TRLD), .TRINR(TRINR), .TRCLR(TRCLR));
  // Enable_ControlUnit enable_controlunit_1: pin names not known; wires that end beside it: decoder4x16_1_p20[13], decoder3x8_1_p11[5], decoder4x16_1_p20[11], decoder4x16_1_p20[15], decoder3x8_1_p11[6], decoder3x8_1_p11[1], decoder4x16_1_p20[10], decoder3x8_1_p11[2], decoder3x8_1_p11[3], decoder3x8_1_p11[7], decoder4x16_1_p20[9], decoder3x8_1_p11[4], and_1_out, IR[10], and_2_out, IR[9], IR[7], IR[6], R, decoder4x16_1_p20[14], ARE, PCE, DRE, ACE, IRE, TRE, MEME
  E_ControlUnit e_controlunit_1 (
    .D1(decoder3x8_1_p11[2]), .T5(decoder4x16_1_p20[10]), .r(and_2_out), .B7(IR[7]), .B6(IR[6]),
    .B10(IR[10]), .B8(IR[8]), .ELD(ELD), .ECLR(ECLR), .ECMP(ECMP));
  IO io_1 (
    .p(and_1_out), .B7(IR[7]), .R(R), .T2(decoder4x16_1_p20[13]), .B6(IR[6]), .s_r(and_2_out), .B0(IR[0]),
    .T0(decoder4x16_1_p20[15]), .T1(decoder4x16_1_p20[14]), .IEN(IEN), .FGI(FGI), .FGO(FGO), .B11(IR[11]),
    .B10(IR[10]), .IENSET(IENSET), .IENCLR(IENCLR), .SCLR(SCLR), .RSET(RSET), .RCLR(RCLR), .FGICLR(FGICLR),
    .FGOCLR(FGOCLR), .CPE(CPE));
  // also tied to GND on the sheet: ALUCin

  // Notes on the sheet:
  //   Operation Decoder
  //   D
  //   Sequence Decoder
  //   T
  //   p = D7 I T3
  //   r = D7 I' T3
endmodule
